# Fritzing sketch Mobile_Radio_Network-Garcia (saved by Fritzing 0.9.3b)
breadboards: 2

parts:
  U1 = XBEE-1 [package=xbee-1_lock]
  Part1 = Arduino Uno (Rev3)
  U3 = XBEE-1 [package=xbee-1_lock]
  T1 = LM35 Temperature Sensor [package="TO92 [THT]"]
  U2 = LIPO-110mAh [package=lipo-110]

nets:
  N1: U1.DOUT, Part1.3V3
  N2: U1.DIN, Part1.D1/TX
  N3: U1.DIO12, Part1.D0/RX
  GND: U1.GND, Part1.GND
  N4: U3.DOUT, T1.+Vs, U2.+
  GND_2: U3.GND, T1.GND, U2.-
  N5: U3.DIO0, T1.Vout
